# Fritzing sketch KSSR22 (saved by Fritzing 0.9.2b)
breadboards: 1

parts:
  Part1 = Arduino Uno (Rev3)
  Part2 = Logic Level Converter
  U1 = ESP8266 WiFi Module [part_number=ESP8266]
  Grove1 = Grove Buzz
  SD_card_module1 = SD Card Module
  R1 = Resistor [tolerance=±5% resistance=1k package=THT]
  S1 = Pushbutton [package="[THT]"]
  R2 = Resistor [tolerance=±5% resistance=1k package=THT]
  R3 = Resistor [tolerance=±5% resistance=1k package=THT]
  LED1 = LED - 5mm [color="Red (633nm)" package="5 mm [THT]"]
  LED2 = LED - 5mm [color="White (4500K)" package="5 mm [THT]"]

nets:
  N1: Part1.A0, Grove1.SIG
  N2: Part1.D8, R2.Pin_0
  N3: Part1.D9_PWM, R3.Pin_0
  N4: Part1.D10_PWM/SS, SD_card_module1.CS
  N5: Part1.D11_PWM/MOSI, SD_card_module1.MOSI
  N6: Part1.D12/MISO, SD_card_module1.MISO
  N7: Part1.D13/SCK, SD_card_module1.SCK
  GND: Part1.GND, Part2.GND, U1.GND, Grove1.GND, SD_card_module1.GND, S1.Pin_4, LED1.cathode, LED2.cathode
  N8: Part1.D2, Part2.TX_HV
  N9: Part1.D3_PWM, Part2.RX_HV
  3V3: Part1.3V3, Part2.LV, U1.VCC, R1.Pin_1
  5V: Part1.5V, Part2.HV, Grove1.VCC, SD_card_module1.+5
  N10: Part2.RX_LV, U1.RXD
  N11: Part2.TX_LV, U1.TXD
  N12: U1.CH_PD, R1.Pin_0
  N13: R2.Pin_1, LED2.anode
  N14: R3.Pin_1, LED1.anode

custom parts:
  ESP8266 WiFi Module: Generic WiFi Module based on the ESP8266 with onboard PCB antenna and UART communications
  SD Card Module: SD Card Module Slot Socket Reader For Arduino ARM MCU
